# Fritzing sketch circuit (saved by Fritzing 0.7.7b)
breadboards: 1

parts:
  RaspberryPi1 = Raspberry Pi Model B
  IC1 = Microchip MCP23008 8-bit I/O expander [part_number=MCP23008 package="DIP (Dual Inline) [THT]"]
  JACK1 = 2.1mm DC Barrel Jack
  M1 = Stepper Motor - Bipolar  # not connected

nets (from the pcb view):
  3V3: RaspberryPi1.3V3, RaspberryPi1.5V
  N1: RaspberryPi1.SDA, IC1.SDA, IC1.Reset, IC1.VDD, JACK1.center
  N2: RaspberryPi1.SCL, RaspberryPi1.GND, RaspberryPi1.#4, RaspberryPi1.TXD, IC1.SCL, IC1.A2, IC1.A1, IC1.A0, IC1.GP6, IC1.GP7, JACK1.sleeve
  N3: RaspberryPi1.RXD, IC1.GP5
  N4: RaspberryPi1.#17, RaspberryPi1.#18, IC1.GP4
  N5: RaspberryPi1.#21, IC1.GP3
  N6: RaspberryPi1.#22, RaspberryPi1.#23, IC1.GP2
  N7: RaspberryPi1.#24, IC1.GP1
  N8: RaspberryPi1.MISO, RaspberryPi1.#25
  N9: RaspberryPi1.SCLK, RaspberryPi1.CS0

custom parts:
  Raspberry Pi Model B: Raspberry Pi (Model B)
  Microchip MCP23008 8-bit I/O expander: Provides 8-bit, general purpose, parallel I/O expansion for I2C bus. Datasheet: http://ww1.microchip.com/downloads/en/devicedoc/21919e.pdf
  2.1mm DC Barrel Jack: 2.1mm DC Barrel Jack with Thru-Hole Connectors (breadboardable)
