# Fritzing sketch raspberrypi_and_ssd1306 (saved by Fritzing 0.7.7b)
breadboards: 1

parts:
  OLED1 = 128x32 SPI Monochrome OLEDDisplay
  RaspberryPi1 = Raspberry Pi Model B

nets:
  N1: OLED1.CS, RaspberryPi1.CS0
  N2: OLED1.RST, RaspberryPi1.TXD
  N3: OLED1.D/C, RaspberryPi1.RXD
  N4: OLED1.CLK, RaspberryPi1.SCLK
  N5: OLED1.DATA, RaspberryPi1.MOSI
  VIN: OLED1.VIN, RaspberryPi1.3V3
  GND: OLED1.GND, RaspberryPi1.GND

custom parts:
  128x32 SPI Monochrome OLEDDisplay: 128x32 SPI OLED Monochrome Display
  Raspberry Pi Model B: Raspberry Pi (Model B)
